# Fritzing sketch hci (saved by Fritzing 0.9.3b)
breadboards: 1

parts:
  Part1 = Arduino Uno (Rev3)
  R1 = Resistor [tolerance=±5% resistance=220 package="1206 [SMD]"]
  LED1 = LED - 3mm [color="Red (633nm)" package="3 mm [THT]"]
  LED2 = LED - 3mm [color="Red (633nm)" package="3 mm [THT]"]
  U2 = POT [package=pot_alpha_rv16af-20]
  J1 = Basic Servo
  RHT1 = Humidity and Temperature Sensor RHT03
  hc-sr1 = hc-sr04
  J2 = Basic Force Sensing Resistor (FSR) [package=THT]
  R2 = Resistor [tolerance=±5% resistance=1k package="2010 [SMD]"]

nets:
  N1: Part1.A0, U2.S
  N2: Part1.A2, J2.pin_1, R2.Pin_1
  N3: Part1.D11_PWM/MOSI, LED1.cathode, LED2.cathode
  N4: Part1.D12/MISO, hc-sr1.Echo
  N5: Part1.D13/SCK, hc-sr1.Trig
  N6: Part1.D4, RHT1.Data-signal
  N7: Part1.D5_PWM, J1.pulse
  VCC: Part1.5V, U2.E, J1.vcc, RHT1.Vcc, hc-sr1.VCC, J2.pin_0
  GND: Part1.GND, R1.Pin_0, U2.A, J1.gnd, RHT1.GND_2, hc-sr1.GND, R2.Pin_0
  N8: R1.Pin_1, LED1.anode, LED2.anode
